// Logisim project BasicLogicGates.circ as structural Verilog: 1 circuit, main circuit main
module main (
  input  A,
  input  A_2,
  input  A_3,
  input  B,
  input  B_2,
  input  A_4,
  input  B_3,
  input  in_8,
  input  A_5,
  input  in_10,
  input  B_4,
  input  A_6,
  input  B_5,
  input  A_7,
  input  B_6,
  input  A_8,
  input  B_7,
  input  A_9,
  input  B_8,
  input  A_10,
  input  B_9,
  output nA,
  output out_23,
  output out_24,
  output A_X_B,
  output nA___nB,
  output nA_X_nB,
  output A_B,
  output XOR___EX_OR,
  output out_30,
  output A_B_2,
  output A_B_3
);

  wire and_2_out, and_3_out, and_4_out, and_5_out, not_2_out, not_3_out, not_4_out, not_5_out, not_6_out,
       not_7_out, not_8_out, not_9_out, or_4_out, undriven, undriven_2, undriven_3, undriven_4;

  not not_1 (nA, A);
  and and_1 (A_X_B, A_4, B_3);
  or or_1 (A_B, A_6, B_5);
  xor xor_1 (XOR___EX_OR, A_7, B_6);
  not not_2 (not_2_out, B_8);
  not not_3 (not_3_out, undriven);
  and and_2 (and_2_out, A_9, not_2_out);
  and and_3 (and_3_out, undriven_2, not_3_out);
  or or_2 (A_B_2, and_2_out, and_3_out);
  not not_4 (not_4_out, A_5);
  not not_5 (not_5_out, B_4);
  nand nand_1 (out_23, A_2, B);
  nand nand_2 (nA_X_nB, not_4_out, not_5_out);
  nor nor_1 (out_24, A_3, B_2);
  not not_6 (not_6_out, in_8);
  not not_7 (not_7_out, in_10);
  or or_3 (nA___nB, not_6_out, not_7_out);
  xnor xnor_1 (out_30, A_8, B_7);
  not not_8 (not_8_out, B_9);
  not not_9 (not_9_out, undriven_3);
  and and_4 (and_4_out, A_10, not_8_out);
  and and_5 (and_5_out, undriven_4, not_9_out);
  or or_4 (or_4_out, and_4_out, and_5_out);
  not not_10 (A_B_3, or_4_out);

  // Notes on the sheet:
  //   NOT
  //   AND
  //   OR
  //   NAND
  //   NAND
  //   NOR
  //   XNOR
endmodule
