// Logisim project DEMULTIPLEXER.circ as structural Verilog: 1 circuit, main circuit main
module main (
  input  Din,
  input  S1,
  input  S0,
  input  E,
  output out_5,
  output out_6,
  output out_7,
  output out_8
);

  wire not_1_out, not_2_out;

  not not_1 (not_1_out, S1);
  not not_2 (not_2_out, S0);
  and and_1 (out_5, E, not_2_out, not_1_out, Din);
  and and_2 (out_6, E, not_2_out, S1, Din);
  and and_3 (out_7, E, S0, not_1_out, Din);
  and and_4 (out_8, E, S0, S1, Din);

  // Notes on the sheet:
  //   S1'
  //   S0'
endmodule
