// Logisim project FULLADDR.circ as structural Verilog: 1 circuit, main circuit main
module main (
  input  Cin,
  input  A,
  input  B,
  output S,
  output COUT
);

  wire and_1_out, and_2_out, and_3_out, undriven, undriven_2, xor_1_out;

  and and_1 (and_1_out, A, B);
  xor xor_1 (xor_1_out, A, B);
  xor xor_2 (S, xor_1_out, Cin);
  and and_2 (and_2_out, undriven_2, A);
  and and_3 (and_3_out, undriven, B);
  or or_1 (COUT, and_2_out, and_3_out, and_1_out);
endmodule
