// Logisim project FULLSUBTRACTOR.circ as structural Verilog: 1 circuit, main circuit main
module main (
  input  A,
  input  B,
  input  BIN,
  output DIFF,
  output BORROW
);

  wire and_1_out, and_2_out, and_3_out, not_1_out, not_2_out, xor_1_out;

  xor xor_1 (xor_1_out, A, B);
  not not_1 (not_1_out, A);
  not not_2 (not_2_out, A);
  xor xor_2 (DIFF, xor_1_out, BIN);
  and and_1 (and_1_out, B, BIN);
  and and_2 (and_2_out, not_1_out, B);
  and and_3 (and_3_out, not_2_out, BIN);
  or or_1 (BORROW, and_1_out, and_2_out, and_3_out);
endmodule
