// Logisim project HALFSUBTRACTOR.circ as structural Verilog: 1 circuit, main circuit main
module main (
  input  A,
  input  B,
  output difference,
  output BORROW
);

  wire not_1_out;

  not not_1 (not_1_out, A);
  xor xor_1 (difference, A, B);
  and and_1 (BORROW, not_1_out, B);
endmodule
